# Fritzing sketch wiring (saved by Fritzing 0.9.3b)
breadboards: 1

parts:
  Part1 = Arduino Uno (Rev3)
  R1 = Resistor [tolerance=±5% resistance=220 package=THT]
  LED1 = LED - 5mm [color="Red (633nm)" package="5 mm [THT]"]
  J1 = Piezo Speaker
  Part2 = Breakout Board for Electret Microphone

nets:
  N1: Part1.D10_PWM/SS, R1.Pin_0
  N2: Part1.D11_PWM/MOSI, J1.pin1
  N3: Part1.D12/MISO, Part2.AUD
  GND: Part1.GND, LED1.cathode, J1.pin2, Part2.GND
  5V: Part1.5V, Part2.VCC
  N4: R1.Pin_1, LED1.anode

notes:
  This is a sound sensor, which triggers the input when a sound is deteced. Most of them have sensitivity controll.
